// Logisim project Lab03_Encoder.circ as structural Verilog: 2 circuits, main circuit main
module main (
  input  in_1,
  input  in_2,
  input  in_3,
  input  in_4,
  input  in_5,
  input  in_6,
  input  in_7,
  input  in_8,
  input  in_9,
  output [3:0] out_10
);

  Encoder encoder_1 (
    .In1(in_1), .In2(in_2), .In3(in_3), .In4(in_4), .In5(in_5), .In6(in_6), .In7(in_7), .In8(in_8),
    .In9(in_9), .Out1(out_10[0]), .Out2(out_10[1]), .Out3(out_10[2]), .Out4(out_10[3]));
  Hex_Digit_Display hex_digit_display_1 (.value(out_10));  // open: dp

  // Notes on the sheet:
  //   Arken Gaisin
  //   February 18, 2018
  //   Lab 03: Nine-line Priority Encoder
endmodule

module Encoder (
  input  In1,
  input  In2,
  input  In3,
  input  In4,
  input  In5,
  input  In6,
  input  In7,
  input  In8,
  input  In9,
  output Out1,
  output Out2,
  output Out3,
  output Out4
);

  wire and_1_out, and_2_out, and_3_out, and_4_out, U1_out, U2_out, U3_out, U4_out, U8_out, U10_out, U11_out,
       U12_out, U16_out;

  nor U16 (U16_out, In8, In9);
  and U1 (U1_out, In1, ~In2, ~In4, ~In6, U16_out);  // AND_Gate
  and U2 (U2_out, In3, ~In4, ~In6, U16_out);  // AND_Gate
  and U3 (U3_out, In5, ~In6, U16_out);  // AND_Gate
  and U4 (U4_out, In7, U16_out);
  and and_1 (and_1_out, In2, ~In4, ~In5, U16_out);  // AND_Gate
  and U5 (and_1_out, In2, ~In4, ~In5, U16_out);  // AND_Gate
  and and_2 (and_2_out, ~In4, ~In5, In3, U16_out);  // AND_Gate
  and U6 (and_2_out, ~In4, ~In5, In3, U16_out);  // AND_Gate
  and and_3 (and_3_out, In6, U16_out);
  and U7 (and_3_out, In6, U16_out);
  and U8 (U8_out, In7, U16_out);
  and and_4 (and_4_out, In4, U16_out);
  and U9 (and_4_out, In4, U16_out);
  and U10 (U10_out, In5, U16_out);
  and U11 (U11_out, In6, U16_out);
  and U12 (U12_out, In7, U16_out);
  or U13 (Out1, U1_out, U2_out, In9, U3_out, U4_out);
  or U14 (Out2, and_1_out, and_2_out, and_3_out, U8_out);
  or U15 (Out3, and_4_out, U10_out, U11_out, U12_out);
  or U17 (Out4, In8, In9);
endmodule
