// Logisim project Lab4_Chronogram.circ as structural Verilog: 7 circuits, main circuit main
module main (
  input  rst,
  input  [2:0] in_2
);

  wire clk_out;
  wire [3:0] universal_1_out1;

  Clock sysclk ();  // open: out
  Clock #(.highDuration(4), .lowDuration(4)) clk (.out(clk_out));
  Universal universal_1 (.clk(clk_out), .rst(rst), .sel(in_2), .Out1(universal_1_out1));
  // Probe on universal_1_out1
  Hex_Digit_Display hex_digit_display_1 (.value(universal_1_out1));  // open: dp

  // Notes on the sheet:
  //   Arken Gaisin
  //   May 24, 2024
  //   Select : 0 - Up
  //   Lab - D-Flip-Flop Counter
  //   1 - Down
  //   2 - Decade
  //   3 - Ring
  //   4 - Johnson
endmodule

module Up (
  input  clck,
  input  rst,
  output [3:0] out_3
);

  wire d_ff_1_qn, d_ff_2_qn, d_ff_3_qn, d_ff_4_qn;

  D_Flip_Flop d_ff_1 (.D(d_ff_1_qn), .clk(clck), .Q(out_3[0]), .Qn(d_ff_1_qn), .reset(rst));  // open: preset
  D_Flip_Flop d_ff_2 (.D(d_ff_2_qn), .clk(d_ff_1_qn), .Q(out_3[1]), .Qn(d_ff_2_qn), .reset(rst));  // open: preset
  D_Flip_Flop d_ff_3 (.D(d_ff_3_qn), .clk(d_ff_2_qn), .Q(out_3[2]), .Qn(d_ff_3_qn), .reset(rst));  // open: preset
  D_Flip_Flop d_ff_4 (.D(d_ff_4_qn), .clk(d_ff_3_qn), .Q(out_3[3]), .Qn(d_ff_4_qn), .reset(rst));  // open: preset
endmodule

module Down (
  input  clk,
  input  rst,
  output [3:0] out_3
);

  wire d_ff_1_qn, d_ff_2_qn, d_ff_3_qn, d_ff_4_qn;

  D_Flip_Flop d_ff_1 (.D(d_ff_1_qn), .clk(clk), .Q(out_3[0]), .Qn(d_ff_1_qn), .preset(rst));  // open: reset
  D_Flip_Flop d_ff_2 (.D(d_ff_2_qn), .clk(out_3[0]), .Q(out_3[1]), .Qn(d_ff_2_qn), .preset(rst));  // open: reset
  D_Flip_Flop d_ff_3 (.D(d_ff_3_qn), .clk(out_3[1]), .Q(out_3[2]), .Qn(d_ff_3_qn), .preset(rst));  // open: reset
  D_Flip_Flop d_ff_4 (.D(d_ff_4_qn), .clk(out_3[2]), .Q(out_3[3]), .Qn(d_ff_4_qn), .preset(rst));  // open: reset
endmodule

module Decade (
  input  clk,
  input  rst,
  output [3:0] OutD
);

  wire and_1_out, d_ff_1_qn, d_ff_2_qn, d_ff_3_qn, d_ff_4_qn, or_1_out;

  or or_1 (or_1_out, rst, and_1_out);
  D_Flip_Flop d_ff_1 (.D(d_ff_1_qn), .clk(clk), .Q(OutD[0]), .Qn(d_ff_1_qn), .reset(or_1_out));  // open: preset
  D_Flip_Flop d_ff_2 (.D(d_ff_2_qn), .clk(d_ff_1_qn), .Q(OutD[1]), .Qn(d_ff_2_qn), .reset(or_1_out));  // open: preset
  D_Flip_Flop d_ff_3 (.D(d_ff_3_qn), .clk(d_ff_2_qn), .Q(OutD[2]), .Qn(d_ff_3_qn), .reset(or_1_out));  // open: preset
  D_Flip_Flop d_ff_4 (.D(d_ff_4_qn), .clk(d_ff_3_qn), .Q(OutD[3]), .Qn(d_ff_4_qn), .reset(or_1_out));  // open: preset
  and and_1 (and_1_out, OutD[3], OutD[1]);
endmodule

module RingCounter (
  input  clk,
  input  rst,
  output [3:0] Ring
);

  D_Flip_Flop d_ff_1 (.D(Ring[3]), .clk(clk), .Q(Ring[0]), .preset(rst));  // open: Qn, reset
  D_Flip_Flop d_ff_2 (.D(Ring[0]), .clk(clk), .Q(Ring[1]), .reset(rst));  // open: Qn, preset
  D_Flip_Flop d_ff_3 (.D(Ring[1]), .clk(clk), .Q(Ring[2]), .reset(rst));  // open: Qn, preset
  D_Flip_Flop d_ff_4 (.D(Ring[2]), .clk(clk), .Q(Ring[3]), .reset(rst));  // open: Qn, preset
endmodule

module JohnsonCounter (
  input  clk,
  input  rst,
  output [3:0] Johnson
);

  wire d_ff_4_qn;

  D_Flip_Flop d_ff_1 (.D(d_ff_4_qn), .clk(clk), .Q(Johnson[0]), .preset(rst));  // open: Qn, reset
  D_Flip_Flop d_ff_2 (.D(Johnson[0]), .clk(clk), .Q(Johnson[1]), .reset(rst));  // open: Qn, preset
  D_Flip_Flop d_ff_3 (.D(Johnson[1]), .clk(clk), .Q(Johnson[2]), .reset(rst));  // open: Qn, preset
  D_Flip_Flop d_ff_4 (.D(Johnson[2]), .clk(clk), .Q(Johnson[3]), .Qn(d_ff_4_qn), .reset(rst));  // open: preset
endmodule

module Universal (
  input  clk,
  input  rst,
  input  [2:0] sel,
  output [3:0] Out1
);

  wire [3:0] decade_1_outd, down_1_out_3, johnsoncounter_1_johnson, ringcounter_1_ring, up_1_out_3;

  Up up_1 (.clck(clk), .rst(rst), .out_3(up_1_out_3));
  JohnsonCounter johnsoncounter_1 (.clk(clk), .rst(rst), .Johnson(johnsoncounter_1_johnson));
  Down down_1 (.clk(clk), .rst(rst), .out_3(down_1_out_3));
  Decade decade_1 (.clk(clk), .rst(rst), .OutD(decade_1_outd));
  RingCounter ringcounter_1 (.clk(clk), .rst(rst), .Ring(ringcounter_1_ring));
  Multiplexer #(.select(3), .width(4)) multiplexer_1 (
    .in0(up_1_out_3), .in1(down_1_out_3), .in2(decade_1_outd), .in3(ringcounter_1_ring),
    .in4(johnsoncounter_1_johnson), .in5(4'b0001), .in6(4'b0001), .in7(4'b0001), .out(Out1), .sel(sel));
endmodule
