// Logisim project Lab_ALU.circ as structural Verilog: 4 circuits, main circuit main
module main (
  input  in_1,
  input  [3:0] in_2,
  input  [3:0] in_3,
  input  [2:0] in_4,
  input  in_5,
  output out_6,
  output out_7,
  output [3:0] out_8
);

  ALU alu_1 (.Cin(in_1), .InA(in_2), .InB(in_3), .Sel(in_4), .Mode(in_5), .COut(out_6), .Cmp(out_7), .ALUOut(out_8));
endmodule

module ALU (
  input  Cin,
  input  [3:0] InA,
  input  [3:0] InB,
  input  [2:0] Sel,
  input  Mode,
  output COut,
  output Cmp,
  output [3:0] ALUOut
);

  wire [3:0] arithmetic_1_arout, logic_1_logout;

  Arithmetic arithmetic_1 (
    .CIn(Cin), .InA(InA), .InB(InB), .Sel(Sel), .ArOut(arithmetic_1_arout), .COut(COut), .Cmp(Cmp));
  Logic logic_1 (.InA(InA), .Inb(InB), .Sel(Sel), .LogOut(logic_1_logout));
  Multiplexer #(.width(4)) multiplexer_1 (.in0(arithmetic_1_arout), .in1(logic_1_logout), .out(ALUOut), .sel(Mode));

  // Notes on the sheet:
  //   Arken Gaisin
  //   Lab04_ALU
  //   May 23, 2024
endmodule

module Arithmetic (
  input  CIn,
  input  [3:0] InA,
  input  [3:0] InB,
  input  [2:0] Sel,
  output [3:0] ArOut,
  output COut,
  output Cmp
);

  wire adder_1_cout, adder_2_cout, adder_3_cout, subtractor_1_bout, subtractor_2_bout, subtractor_3_bout,
       subtractor_4_bout;
  wire [3:0] adder_1_out, adder_2_out, adder_3_out, multiplier_1_out, multiplier_2_out, not_1_out, not_2_out,
       subtractor_1_out, subtractor_2_out, subtractor_3_out, subtractor_4_out;

  assign not_1_out = ~InB;  // NOT_Gate not_1, 4 bits wide
  Adder #(.width(4)) adder_1 (.a(InA), .b(InB), .out(adder_1_out), .cin(CIn), .cout(adder_1_cout));
  Subtractor #(.width(4)) subtractor_1 (.a(InA), .b(InB), .out(subtractor_1_out), .bin(CIn), .bout(subtractor_1_bout));
  Multiplier #(.width(4)) multiplier_1 (.a(InA), .b(InB), .out(multiplier_1_out));  // open: cin, cout
  Multiplier #(.width(4)) multiplier_2 (.a(InA), .b(not_1_out), .out(multiplier_2_out));  // open: cin, cout
  Adder #(.width(4)) adder_2 (.a(InA), .b(InA), .out(adder_2_out), .cin(CIn), .cout(adder_2_cout));
  Adder #(.width(4)) adder_3 (.a(InA), .b(4'b0001), .out(adder_3_out), .cin(CIn), .cout(adder_3_cout));
  Comparator #(.width(4)) comparator_1 (.a(InA), .b(InB), .eq(Cmp));  // open: gt, lt
  Subtractor #(.width(4)) subtractor_2 (
    .a(InA), .b(4'b0001), .out(subtractor_2_out), .bin(CIn), .bout(subtractor_2_bout));
  Subtractor #(.width(4)) subtractor_3 (
    .a(multiplier_1_out), .b(4'b0001), .out(subtractor_3_out), .bout(subtractor_3_bout));  // open: bin
  Subtractor #(.width(4)) subtractor_4 (
    .a(multiplier_2_out), .b(4'b0001), .out(subtractor_4_out), .bout(subtractor_4_bout));  // open: bin
  assign not_2_out = ~4'b0001;  // NOT_Gate not_2, 4 bits wide
  Multiplexer #(.select(3), .width(4)) multiplexer_1 (
    .in0(not_2_out), .in1(subtractor_2_out), .in2(adder_1_out), .in3(subtractor_1_out),
    .in4(subtractor_3_out), .in5(subtractor_4_out), .in6(adder_2_out), .in7(adder_3_out), .out(ArOut),
    .sel(Sel));
  Multiplexer #(.select(3)) multiplexer_2 (
    .in0(1'b0), .in1(subtractor_2_bout), .in2(adder_1_cout), .in3(subtractor_1_bout),
    .in4(subtractor_3_bout), .in5(subtractor_4_bout), .in6(adder_2_cout), .in7(adder_3_cout), .out(COut),
    .sel(Sel));
endmodule

module Logic (
  input  [3:0] InA,
  input  [3:0] Inb,
  input  [2:0] Sel,
  output [3:0] LogOut
);

  wire [3:0] and_1_out, and_2_out, not_1_out, not_2_out, not_3_out, not_4_out, or_1_out, or_2_out, xor_1_out;

  assign not_1_out = ~Inb;  // NOT_Gate not_1, 4 bits wide
  assign and_1_out = InA & Inb;  // AND_Gate and_1, 4 bits wide
  assign or_1_out = InA | Inb;  // OR_Gate or_1, 4 bits wide
  assign xor_1_out = InA ^ Inb;  // XOR_Gate xor_1, 4 bits wide
  assign and_2_out = InA & not_1_out;  // AND_Gate and_2, 4 bits wide
  assign or_2_out = InA | not_1_out;  // OR_Gate or_2, 4 bits wide
  assign not_2_out = ~or_1_out;  // NOT_Gate not_2, 4 bits wide
  assign not_3_out = ~and_1_out;  // NOT_Gate not_3, 4 bits wide
  assign not_4_out = ~InA;  // NOT_Gate not_4, 4 bits wide
  Multiplexer #(.select(3), .width(4)) multiplexer_1 (
    .in0(and_1_out), .in1(not_3_out), .in2(or_1_out), .in3(not_2_out), .in4(xor_1_out), .in5(and_2_out),
    .in6(or_2_out), .in7(not_4_out), .out(LogOut), .sel(Sel));

  // Notes on the sheet:
  //   Logic Subcircuit
  //   0 = AB
  //   1 = (AB)'
  //   2 = A+B
  //   5 = AB'
  //   6 = A+B'
  //   7 = A'
  //   3 = (A+B)'
  //   4 = A Xor B
endmodule
