// Logisim project tutorial_introduction.circ as structural Verilog: 1 circuit, main circuit main
module main (
  input  input_A,
  input  input_B,
  output output_C
);

  wire and_1_out, and_2_out, not_1_out, not_2_out;

  not not_1 (not_1_out, input_B);
  not not_2 (not_2_out, input_A);
  and and_1 (and_1_out, input_A, not_1_out);
  and and_2 (and_2_out, not_2_out, input_B);
  or or_1 (output_C, and_1_out, and_2_out);
endmodule
